# Fritzing sketch Camera control Sketch bread v1 (saved by Fritzing 0.9.3b)
circuit board: 9.92456cm x 7.23752cm
breadboards: 2

parts:
  C8 = Electrolytic Capacitor [capacitance=10µF rated_voltage=35V package="100 mil [THT, electrolytic]"]
  C9 = Electrolytic Capacitor [capacitance=10µF rated_voltage=35V package="100 mil [THT, electrolytic]"]
  U3 = Voltage Regulator - 5V [package="TO220 [THT]"]
  R1 = Resistor [tolerance=±5% resistance=220 package=THT]
  U4 = atmega328 [package=dip]
  XTAL3 = Crystal [frequency="16 Mhz" package=THT]
  C12 = Ceramic Capacitor [capacitance=22pF rated_voltage=35V package="200 mil [THT, multilayer]"]
  C13 = Ceramic Capacitor [capacitance=22pF rated_voltage=35V package="200 mil [THT, multilayer]"]
  RESET = Pushbutton [package="[THT]"]
  R5 = Resistor [tolerance=±5% resistance=10k package=THT]
  U5 = LCD-16X2 [package=lcd-16x2]
  R6 = TRIMPOT [package=trimpot_pth_s3_lock]
  R7 = Resistor [tolerance=±5% resistance=220 package=THT]
  R8 = Resistor [tolerance=±5% resistance=2k package=THT]
  R9 = Resistor [tolerance=±5% resistance=330 package=THT]
  R10 = Resistor [tolerance=±5% resistance=680 package=THT]
  R11 = Resistor [tolerance=±5% resistance=3.6k package=THT]
  JL = Screw terminal - 2 pins [package=THT]
  JU = Screw terminal - 2 pins [package=THT]
  JD = Screw terminal - 2 pins [package=THT]
  JR = Screw terminal - 2 pins [package=THT]
  COMM = screw terminal, 4 pins
  J2 = Screw terminal - 2 pins [package=THT]
  U6 = Optocoupler [package=THT]
  R12 = Resistor [tolerance=±5% resistance=220 package=THT]
  U7 = Optocoupler [package=THT]
  R13 = Resistor [tolerance=±5% resistance=220 package=THT]
  Shot = Screw terminal - 2 pins [package=THT]
  Focus = Screw terminal - 2 pins [package=THT]
  ON = LED - 3mm [color="Red (633nm)" package="3 mm [THT]"]
  LEDshot = LED - 3mm [color="Green (555nm)" package="3 mm [THT]"]
  LEDfocus = LED - 3mm [color="Yellow (595nm)" package="3 mm [THT]"]
  Sound = Audio Jack (TRS) 3.5mm [package="4Ucon 08780 [THT]"]
  Light = Audio Jack (TRS) 3.5mm [package="4Ucon 08780 [THT]"]
  R15 = Resistor [tolerance=±5% resistance=10k package=THT]
  R16 = Resistor [tolerance=±5% resistance=10k package=THT]

nets:
  GND: C8.-, C9.-, U3.GND, U4.GND, C12.1, C13.1, RESET.Pin_3, RESET.Pin_4, U5.VSS, U5.R_W, R6.CCW, R7.Pin_0, R8.Pin_0, JL.pin1, JU.pin1, JD.pin1, JR.pin1, J2.pin2, U6.Pin_2, U7.Pin_2, ON.cathode, LEDshot.cathode, LEDfocus.cathode, R15.Pin_0, R16.Pin_0
  N1: C8.+, U3.input_voltage, J2.pin1
  VCC: C9.+, U3.output_voltage, R1.Pin_1, U4.VCC, U4.AVCC, R5.Pin_1, U5.VDD, U5.K, R6.CW, Sound.Ring, Sound.Tip, Light.Ring, Light.Tip
  N2: R1.Pin_0, ON.anode
  N3: U4.RESET, RESET.Pin_1, RESET.Pin_2, R5.Pin_0, COMM.pin1
  N4: U4.D2, U5.RS
  N5: U4.D3_(PWM), U5.E
  N6: U4.D4, U5.DB4
  N7: U4.XLAT1, XTAL3.pin_0, C12.0
  N8: U4.XLAT2, XTAL3.pin_1, C13.0
  N9: U4.D5_(PWM), U5.DB5
  N10: U4.D6_(PWM), U5.DB6
  N11: U4.D7, U5.DB7
  N12: U4.D9_(PWM), R13.Pin_1
  N13: U4.D10_(PWM), R12.Pin_1
  N14: U4.D11_(PWM), COMM.pin4
  N15: U4.D12, COMM.pin3
  N16: U4.D13, COMM.pin2
  N17: U4.A0, R8.Pin_1, R9.Pin_0, JL.pin2
  N18: U4.A1, Light.Sleeve, R15.Pin_1
  N19: U4.A2, Sound.Sleeve, R16.Pin_1
  N20: U5.VO, R6.WIPER
  N21: U5.A, R7.Pin_1
  N22: R9.Pin_1, R10.Pin_0, JU.pin2
  N23: R10.Pin_1, R11.Pin_0, JD.pin2
  N24: R11.Pin_1, JR.pin2
  N25: U6.Pin_1, R12.Pin_0, LEDfocus.anode
  N26: U6.Pin_4, Focus.pin1
  N27: U6.Pin_5, Focus.pin2
  N28: U7.Pin_1, R13.Pin_0, LEDshot.anode
  N29: U7.Pin_4, Shot.pin1
  N30: U7.Pin_5, Shot.pin2

notes:
  Camera CTR - Design by Renato Brant
  PCB v1.0
  9V
  -
  +
  Focus
  Left
  Up
  Down
  Right
  2k
  680
  330
  3.6k
  10k
  220
  Shot
  ATmega328-20pu
  7805
  10µ
  16Mhz
  22p
  13
  12
  11
  10
