# Fritzing sketch Camera control Sketch bread v2.0 (saved by Fritzing 0.9.3b)
circuit board: 10cm x 4cm
breadboards: 2

parts:
  C8 = Electrolytic Capacitor [capacitance=10µF rated_voltage=35V package="100 mil [THT, electrolytic]"]
  C9 = Electrolytic Capacitor [capacitance=10µF rated_voltage=35V package="100 mil [THT, electrolytic]"]
  U3 = Voltage Regulator - 5V [package="TO220 [THT]"]
  R1 = Resistor [tolerance=±5% resistance=220 package=THT]
  U4 = atmega328 [package=dip]
  XTAL3 = Crystal [frequency="16 Mhz" package=THT]
  C12 = Ceramic Capacitor [capacitance=22pF rated_voltage=35V package="200 mil [THT, multilayer]"]
  C13 = Ceramic Capacitor [capacitance=22pF rated_voltage=35V package="200 mil [THT, multilayer]"]
  RESET = Pushbutton [package="[THT]"]
  R5 = Resistor [tolerance=±5% resistance=10k package=THT]
  U5 = LCD-16X2 [package=lcd-16x2]
  R7 = Resistor [tolerance=±5% resistance=220 package=THT]
  R8 = Resistor [tolerance=±5% resistance=2k package=THT]
  R9 = Resistor [tolerance=±5% resistance=330 package=THT]
  R10 = Resistor [tolerance=±5% resistance=680 package=THT]
  R11 = Resistor [tolerance=±5% resistance=3.6k package=THT]
  JL = Screw terminal - 2 pins [package=THT]
  JU = Screw terminal - 2 pins [package=THT]
  JD = Screw terminal - 2 pins [package=THT]
  JR = Screw terminal - 2 pins [package=THT]
  COMM = screw terminal, 4 pins
  5-12V = Screw terminal - 2 pins [package=THT]
  Optoacoplador_2 = Optocoupler [package=THT]
  R12 = Resistor [tolerance=±5% resistance=220 package=THT]
  Optoacoplador_1 = Optocoupler [package=THT]
  R13 = Resistor [tolerance=±5% resistance=220 package=THT]
  ON = LED - 3mm [color="Red (633nm)" package="3 mm [THT]"]
  LEDshot = LED - 3mm [color="Green (555nm)" package="3 mm [THT]"]
  LEDfocus = LED - 3mm [color="Yellow (595nm)" package="3 mm [THT]"]
  R15 = Resistor [tolerance=±5% resistance=10k package=THT]
  R6 = TRIMPOT [package=trimpot_pth_s3_lock]
  Shot = screw terminal, 3 pins
  Light = Screw terminal - 2 pins [package=THT]
  Sound = screw terminal, 3 pins

nets:
  GND: C8.-, C9.-, U3.GND, U4.GND, C12.1, C13.1, RESET.Pin_3, RESET.Pin_4, U5.VSS, U5.R_W, R7.Pin_0, JL.pin1, JU.pin1, JD.pin1, JR.pin1, 5-12V.pin2, ON.cathode, LEDshot.cathode, LEDfocus.cathode, R15.Pin_0, R6.CCW, Sound.pin1
  N1: C8.+, U3.input_voltage, 5-12V.pin1
  +5: C9.+, U3.output_voltage, R1.Pin_1, U4.VCC, U4.AVCC, R5.Pin_1, U5.VDD, U5.K, R8.Pin_0, R6.CW, Light.pin1, Sound.pin3
  N2: R1.Pin_0, ON.anode
  RESET: U4.RESET, RESET.Pin_1, RESET.Pin_2, R5.Pin_0, COMM.pin1
  D2: U4.D2, U5.RS
  D3: U4.D3_(PWM), U5.E
  D4: U4.D4, U5.DB4
  N3: U4.XLAT1, XTAL3.pin_0, C12.0
  N4: U4.XLAT2, XTAL3.pin_1, C13.0
  D5: U4.D5_(PWM), U5.DB5
  D6: U4.D6_(PWM), U5.DB6
  D7: U4.D7, U5.DB7
  D9: U4.D9_(PWM), R13.Pin_1
  D10: U4.D10_(PWM), R12.Pin_1
  D11: U4.D11_(PWM), COMM.pin4
  D12: U4.D12, COMM.pin3
  D13: U4.D13, COMM.pin2
  A0: U4.A0, R8.Pin_1, R9.Pin_0, JL.pin2
  A1: U4.A1, R15.Pin_1, Light.pin2
  A2: U4.A2, Sound.pin2
  N5: U5.VO, R6.WIPER
  N6: U5.A, R7.Pin_1
  N7: R9.Pin_1, R10.Pin_0, JU.pin2
  N8: R10.Pin_1, R11.Pin_0, JD.pin2
  N9: R11.Pin_1, JR.pin2
  N10: Optoacoplador_2.Pin_1, R12.Pin_0
  N11: Optoacoplador_2.Pin_2, LEDfocus.anode
  N12: Optoacoplador_2.Pin_4, Optoacoplador_1.Pin_5, Shot.pin2
  N13: Optoacoplador_2.Pin_5, Shot.pin1
  N14: Optoacoplador_1.Pin_1, R13.Pin_0
  N15: Optoacoplador_1.Pin_2, LEDshot.anode
  N16: Optoacoplador_1.Pin_4, Shot.pin3

notes:
  9V
  -
  +
  Left
  Up
  Down
  Right
  2k
  680
  330
  3.6k
  10k
  220
  ATmega328-20pu
  7805
  10µ
  16Mhz
  22p
  13
  12
  11
  10
  Camera CTR
  PCB v2.0
  Renato Brant
  Botão L = 000 <020
  Botão U = 141 <240
  Botão D = 341 <693
  Botão R = 713 <900
  Focus/Shot
  PCBv2.0
