# Fritzing sketch Camera control Sketch bread v2.x (saved by Fritzing 0.9.3b)
breadboards: 2

parts:
  R1 = Resistor [tolerance=±5% resistance=220 package=THT]
  XTAL3 = Crystal [frequency="16 Mhz" package=THT]
  C8 = Electrolytic Capacitor [capacitance=10µF package="100 mil [THT, electrolytic]"]
  C13 = Ceramic Capacitor [capacitance=22pF package="200 mil [THT, multilayer]"]
  C9 = Electrolytic Capacitor [capacitance=10µF package="100 mil [THT, electrolytic]"]
  U5 = LCD-16X2 [package=lcd-16x2]
  JR = Screw terminal - 2 pins [package=THT]
  U4 = atmega328 [package=dip]
  LEDshot = LED - 3mm [color="Green (555nm)" package="3 mm [THT]"]
  Light = Screw terminal - 2 pins [package=THT]
  Optoacoplador_2 = Optocoupler [package=THT]
  5-12V = Screw terminal - 2 pins [package=THT]
  JD = Screw terminal - 2 pins [package=THT]
  R6 = TRIMPOT [package=trimpot_pth_s3_lock]
  R13 = Resistor [tolerance=±5% resistance=220 package=THT]
  Sound = screw terminal, 3 pins
  R5 = Resistor [tolerance=±5% resistance=10k package=THT]
  U3 = Voltage Regulator - 5V [package="TO220 [THT]"]
  C12 = Ceramic Capacitor [capacitance=22pF package="200 mil [THT, multilayer]"]
  R12 = Resistor [tolerance=±5% resistance=220 package=THT]
  JL = Screw terminal - 2 pins [package=THT]
  R15 = Resistor [tolerance=±5% resistance=10k package=THT]
  R8 = Resistor [tolerance=±5% resistance=2k package=THT]
  LEDfocus = LED - 3mm [color="Yellow (595nm)" package="3 mm [THT]"]
  ON = LED - 3mm [color="Red (633nm)" package="3 mm [THT]"]
  R7 = Resistor [tolerance=±5% resistance=220 package=THT]
  JU = Screw terminal - 2 pins [package=THT]
  Optoacoplador_1 = Optocoupler [package=THT]
  R11 = Resistor [tolerance=±5% resistance=3.6k package=THT]
  RESET = Pushbutton [package="[THT]"]
  R10 = Resistor [tolerance=±5% resistance=680 package=THT]
  R9 = Resistor [tolerance=±5% resistance=330 package=THT]
  Shot = screw terminal, 3 pins

nets:
  N1: R1.Pin_0, ON.anode
  +5: R1.Pin_1, C9.+, U5.VDD, U5.K, U4.VCC, U4.AVCC, Light.pin1, R6.CW, Sound.pin3, R5.Pin_1, U3.output_voltage, R8.Pin_0
  N2: XTAL3.pin_0, U4.XLAT1, C12.0
  N3: XTAL3.pin_1, C13.0, U4.XLAT2
  GND: C8.-, C13.1, C9.-, U5.VSS, U5.R_W, JR.pin1, U4.GND, LEDshot.cathode, 5-12V.pin2, JD.pin1, R6.CCW, Sound.pin1, U3.GND, C12.1, JL.pin1, R15.Pin_0, LEDfocus.cathode, ON.cathode, R7.Pin_0, JU.pin1, RESET.Pin_3
  N4: C8.+, 5-12V.pin1, U3.input_voltage
  N5: U5.VO, R6.WIPER
  D2: U5.RS, U4.D2
  D3: U5.E, U4.D3_(PWM)
  D4: U5.DB4, U4.D4
  D5: U5.DB5, U4.D5_(PWM)
  D6: U5.DB6, U4.D6_(PWM)
  D7: U5.DB7, U4.D7
  N6: U5.A, R7.Pin_1
  N7: JR.pin2, R11.Pin_1
  RESET: U4.RESET, R5.Pin_0, RESET.Pin_1, RESET.Pin_2
  D9: U4.D9_(PWM), R13.Pin_1
  D10: U4.D10_(PWM), R12.Pin_1
  D11: U4.D11_(PWM)
  D12: U4.D12
  D13: U4.D13
  A3: U4.A3, JL.pin2, R8.Pin_1, R9.Pin_0
  A4: U4.A4, Sound.pin2
  A5: U4.A5, Light.pin2, R15.Pin_1
  N8: LEDshot.anode, Optoacoplador_1.Pin_2
  N9: Optoacoplador_2.Pin_1, R12.Pin_0
  N10: Optoacoplador_2.Pin_2, LEDfocus.anode
  N11: Optoacoplador_2.Pin_4, Optoacoplador_1.Pin_5, Shot.pin2
  N12: Optoacoplador_2.Pin_5, Shot.pin1
  N13: JD.pin2, R11.Pin_0, R10.Pin_1
  N14: R13.Pin_0, Optoacoplador_1.Pin_1
  N15: JU.pin2, R10.Pin_0, R9.Pin_1
  N16: Optoacoplador_1.Pin_4, Shot.pin3

notes:
  Botão L = 000 <020
  Botão U = 141 <240
  Botão D = 341 <693
  Botão R = 713 <900
  Right
  Down
  Left
  Up
