# Fritzing sketch Camera control Sketch bread v4 (saved by Fritzing 0.9.3b)
circuit board: 4.68726cm x 7.75302cm

parts:
  C8 = Electrolytic Capacitor [capacitance=10µF rated_voltage=35V package="100 mil [THT, electrolytic]"]
  C9 = Electrolytic Capacitor [capacitance=10µF rated_voltage=35V package="100 mil [THT, electrolytic]"]
  U3 = Voltage Regulator - 5V [package="TO220 [THT]"]
  R1 = Resistor [tolerance=±5% resistance=220 package=THT]
  R8 = Resistor [tolerance=±5% resistance=2k package=THT]
  R9 = Resistor [tolerance=±5% resistance=330 package=THT]
  R10 = Resistor [tolerance=±5% resistance=680 package=THT]
  R11 = Resistor [tolerance=±5% resistance=3.6k package=THT]
  Optoacoplador_2 = Optocoupler [package=THT]
  Optoacoplador_1 = Optocoupler [package=THT]
  R13 = Resistor [tolerance=±5% resistance=220 package=THT]
  ON = LED - 3mm [color="Red (633nm)" package="3 mm [THT]"]
  LEDshot = LED - 3mm [color="Green (555nm)" package="3 mm [THT]"]
  LEDfocus = LED - 3mm [color="Yellow (595nm)" package="3 mm [THT]"]
  R15 = Resistor [tolerance=±5% resistance=10k package=THT]
  Part2 = Arduino Pro Mini (3.3V)
  Sound = screw terminal, 3 pins
  Light = Screw terminal - 2 pins [package=THT]
  UP = Pushbutton [package="[THT]"]
  RIGHT = Pushbutton [package="[THT]"]
  DOWN = Pushbutton [package="[THT]"]
  LEFT = Pushbutton [package="[THT]"]
  5-12V = Screw terminal - 2 pins [package=THT]
  Shot = screw terminal, 3 pins
  Squix1 = OLED 0.96" 128x64 I2C SSD1306
  R12 = Resistor [tolerance=±5% resistance=220 package=THT]

nets:
  GND: C8.-, C9.-, U3.GND, ON.cathode, LEDshot.cathode, LEDfocus.cathode, R15.Pin_0, Part2.GND, Sound.pin1, UP.Pin_3, UP.Pin_4, LEFT.Pin_3, LEFT.Pin_4, 5-12V.pin2, Squix1.GND
  N1: C8.+, U3.input_voltage, 5-12V.pin1
  +5: C9.+, U3.output_voltage, R1.Pin_1, R8.Pin_0, Part2.VCC, Sound.pin3, Light.pin1, Squix1.VCC
  N2: R1.Pin_0, ON.anode
  A1: R8.Pin_1, R9.Pin_0, Part2.A1, LEFT.Pin_1
  N3: R9.Pin_1, R10.Pin_0, UP.Pin_1, UP.Pin_2
  N4: R10.Pin_1, R11.Pin_0, DOWN.Pin_1
  N5: R11.Pin_1, RIGHT.Pin_1
  N6: Optoacoplador_2.Pin_1, R12.Pin_0
  N7: Optoacoplador_2.Pin_2, LEDfocus.anode
  N8: Optoacoplador_2.Pin_4, Optoacoplador_1.Pin_5, Shot.pin2
  N9: Optoacoplador_2.Pin_5, Shot.pin1
  N10: Optoacoplador_1.Pin_1, R13.Pin_0
  N11: Optoacoplador_1.Pin_2, LEDshot.anode
  N12: Optoacoplador_1.Pin_4, Shot.pin3
  D4: R13.Pin_1, Part2.D4
  A0: R15.Pin_1, Part2.A0, Light.pin2
  N13: Part2.A4, Squix1.SCA
  N14: Part2.A5, Squix1.SCL
  A6: Part2.A6, Sound.pin2
  D13: Part2.SCK
  D12: Part2.MISO
  D11: Part2.MOSI
  D6: Part2.D6
  D5: Part2.D5
  D3: Part2.D3, R12.Pin_1
  D2: Part2.D2
  RESET: Part2.RESET
  N15: RIGHT.Pin_3, DOWN.Pin_3

notes:
  2k
  680
  330
  3.6k
  Botão L = 000 <020
  Botão U = 141 <240
  Botão D = 341 <693
  Botão R = 713 <900
